// Logisim project computer.circ as structural Verilog
module semiadder (
  input  A,
  input  B,
  output U,
  output S
);

  and and_1 (U, A, B);
  xor xor_1 (S, A, B);
endmodule

module fulladder (
  input  A,
  input  B,
  input  D,
  output U,
  output S
);

  wire semiadder_1_s, semiadder_1_u, semiadder_2_u;

  semiadder semiadder_1 (.A(A), .B(B), .U(semiadder_1_u), .S(semiadder_1_s));
  semiadder semiadder_2 (.A(semiadder_1_s), .B(D), .U(semiadder_2_u), .S(S));
  or or_1 (U, semiadder_1_u, semiadder_2_u);
endmodule

module Add_8 (
  input  A0,
  input  A1,
  input  A2,
  input  A3,
  input  A4,
  input  A5,
  input  A6,
  input  AN,
  input  B0,
  input  B1,
  input  B2,
  input  B3,
  input  B4,
  input  B5,
  input  B6,
  input  BN,
  output S0,
  output S1,
  output S2,
  output S3,
  output S4,
  output S5,
  output S6,
  output SN,
  output SO
);

  wire fulladder_1_u, fulladder_2_u, fulladder_3_u, fulladder_4_u, fulladder_5_u, fulladder_6_u,
       semiadder_1_u;

  semiadder semiadder_1 (.A(A0), .B(B0), .U(semiadder_1_u), .S(S0));
  fulladder fulladder_1 (.A(A1), .B(B1), .D(semiadder_1_u), .U(fulladder_1_u), .S(S1));
  fulladder fulladder_2 (.A(A2), .B(B2), .D(fulladder_1_u), .U(fulladder_2_u), .S(S2));
  fulladder fulladder_3 (.A(A3), .B(B3), .D(fulladder_2_u), .U(fulladder_3_u), .S(S3));
  fulladder fulladder_4 (.A(A4), .B(B4), .D(fulladder_3_u), .U(fulladder_4_u), .S(S4));
  fulladder fulladder_5 (.A(A5), .B(B5), .D(fulladder_4_u), .U(fulladder_5_u), .S(S5));
  fulladder fulladder_6 (.A(A6), .B(B6), .D(fulladder_5_u), .U(fulladder_6_u), .S(S6));
  fulladder fulladder_7 (.A(AN), .B(BN), .D(fulladder_6_u), .U(SO), .S(SN));
endmodule

module Sel_2 (
  input  _0,
  input  _1,
  input  S,
  output U
);

  wire and_1_out, and_2_out, not_1_out;

  and and_1 (and_1_out, _0, not_1_out);
  not not_1 (not_1_out, S);
  and and_2 (and_2_out, _1, S);
  or or_1 (U, and_1_out, and_2_out);
endmodule

module Sel_8 (
  input  A0,
  input  A1,
  input  A2,
  input  A3,
  input  A4,
  input  A5,
  input  A6,
  input  AN,
  input  B0,
  input  B1,
  input  B2,
  input  B3,
  input  B4,
  input  B5,
  input  S,
  input  B6,
  input  BN,
  output S0,
  output S1,
  output S2,
  output S3,
  output S4,
  output S5,
  output S6,
  output SN
);

  Sel_2 sel_2_1 (._0(A0), ._1(B0), .S(S), .U(S0));
  Sel_2 sel_2_2 (._0(A1), ._1(B1), .S(S), .U(S1));
  Sel_2 sel_2_3 (._0(A2), ._1(B2), .S(S), .U(S2));
  Sel_2 sel_2_4 (._0(A3), ._1(B3), .S(S), .U(S3));
  Sel_2 sel_2_5 (._0(A4), ._1(B4), .S(S), .U(S4));
  Sel_2 sel_2_6 (._0(A5), ._1(B5), .S(S), .U(S5));
  Sel_2 sel_2_7 (._0(A6), ._1(B6), .S(S), .U(S6));
  Sel_2 sel_2_8 (._0(AN), ._1(BN), .S(S), .U(SN));
endmodule

module Sel_8_M (
  input  [7:0] A,
  input  [7:0] B,
  input  S,
  output [7:0] S_2
);

  Sel_2 sel_2_1 (._0(A[0]), ._1(B[0]), .S(S), .U(S_2[0]));
  Sel_2 sel_2_2 (._0(A[1]), ._1(B[1]), .S(S), .U(S_2[1]));
  Sel_2 sel_2_3 (._0(A[2]), ._1(B[2]), .S(S), .U(S_2[2]));
  Sel_2 sel_2_4 (._0(A[3]), ._1(B[3]), .S(S), .U(S_2[3]));
  Sel_2 sel_2_5 (._0(A[4]), ._1(B[4]), .S(S), .U(S_2[4]));
  Sel_2 sel_2_6 (._0(A[5]), ._1(B[5]), .S(S), .U(S_2[5]));
  Sel_2 sel_2_7 (._0(A[6]), ._1(B[6]), .S(S), .U(S_2[6]));
  Sel_2 sel_2_8 (._0(A[7]), ._1(B[7]), .S(S), .U(S_2[7]));
endmodule

module SW_8 (
  input  A0,
  input  A1,
  input  A2,
  input  A3,
  input  A4,
  input  A5,
  input  S,
  input  A6,
  input  AN,
  output S0,
  output S1,
  output S2,
  output S3,
  output S4,
  output S5,
  output S6,
  output SN
);

  Sel_8 sel_8_1 (
    .A0(1'b0), .A1(1'b0), .A2(1'b0), .A3(1'b0), .A4(1'b0), .A5(1'b0), .A6(1'b0), .AN(1'b0), .B0(A0), .B1(A1),
    .B2(A2), .B3(A3), .B4(A4), .B5(A5), .B6(A6), .BN(AN), .S(S), .S0(S0), .S1(S1), .S2(S2), .S3(S3), .S4(S4),
    .S5(S5), .S6(S6), .SN(SN));
endmodule

module SW_8_M (
  input  [7:0] B,
  input  S,
  output [7:0] S_2
);

  Sel_8 sel_8_1 (
    .A0(1'b0), .A1(1'b0), .A2(1'b0), .A3(1'b0), .A4(1'b0), .A5(1'b0), .A6(1'b0), .AN(1'b0), .B0(B[0]),
    .B1(B[1]), .B2(B[2]), .B3(B[3]), .B4(B[4]), .B5(B[5]), .B6(B[6]), .BN(B[7]), .S(S), .S0(S_2[0]),
    .S1(S_2[1]), .S2(S_2[2]), .S3(S_2[3]), .S4(S_2[4]), .S5(S_2[5]), .S6(S_2[6]), .SN(S_2[7]));
endmodule

module D_Flip_Flop (
  input  S,
  input  D,
  input  CLK,
  input  E,
  input  R,
  output U,
  output nU
);

  wire and_1_out, and_2_out, and_3_out, and_4_out, and_5_out, and_6_out, nor_1_out, nor_2_out, nor_3_out;

  and and_1 (and_1_out, CLK, S);
  and and_2 (and_2_out, D, CLK);
  and and_3 (and_3_out, CLK, E);
  and and_4 (and_4_out, CLK, R);
  nor nor_1 (nor_1_out, and_1_out, and_4_out);
  and and_5 (and_5_out, and_2_out, and_3_out, nor_1_out);
  and and_6 (and_6_out, nor_1_out, ~and_2_out, and_3_out);  // AND_Gate
  nor nor_2 (nor_2_out, and_1_out, and_5_out);
  nor nor_3 (nor_3_out, and_6_out, and_4_out);
  nand nand_1 (U, nor_2_out, nU);
  nand nand_2 (nU, U, nor_3_out);
endmodule

module D_8 (
  input  [7:0] D,
  input  CLK,
  input  E,
  output [7:0] U
);

  D_Flip_Flop d_ff_1 (.D(D[0]), .CLK(CLK), .E(E), .S(1'b0), .R(1'b0), .U(U[0]));  // open: nU
  D_Flip_Flop d_ff_2 (.D(D[1]), .CLK(CLK), .E(E), .S(1'b0), .R(1'b0), .U(U[1]));  // open: nU
  D_Flip_Flop d_ff_3 (.D(D[2]), .CLK(CLK), .E(E), .S(1'b0), .R(1'b0), .U(U[2]));  // open: nU
  D_Flip_Flop d_ff_4 (.D(D[3]), .CLK(CLK), .E(E), .S(1'b0), .R(1'b0), .U(U[3]));  // open: nU
  D_Flip_Flop d_ff_5 (.D(D[4]), .CLK(CLK), .E(E), .S(1'b0), .R(1'b0), .U(U[4]));  // open: nU
  D_Flip_Flop d_ff_6 (.D(D[5]), .CLK(CLK), .E(E), .S(1'b0), .R(1'b0), .U(U[5]));  // open: nU
  D_Flip_Flop d_ff_7 (.D(D[6]), .CLK(CLK), .E(E), .S(1'b0), .R(1'b0), .U(U[6]));  // open: nU
  D_Flip_Flop d_ff_8 (.D(D[7]), .CLK(CLK), .E(E), .S(1'b0), .R(1'b0), .U(U[7]));  // open: nU
endmodule

module Div_2 (
  input  S,
  input  _0,
  output U0,
  output U1
);

  wire not_1_out;

  not not_1 (not_1_out, S);
  and and_1 (U0, not_1_out, _0);
  and and_2 (U1, _0, S);
endmodule

module Merger_8 (
  input  A0,
  input  A1,
  input  A2,
  input  A3,
  input  A4,
  input  A5,
  input  A6,
  input  AN,
  input  B0,
  input  B1,
  input  B2,
  input  B3,
  input  B4,
  input  B5,
  input  B6,
  input  BN,
  output S0,
  output S1,
  output S2,
  output S3,
  output S4,
  output S5,
  output S6,
  output SN
);

  or or_1 (S0, A0, B0);
  or or_2 (S1, A1, B1);
  or or_3 (S2, A2, B2);
  or or_4 (S3, A3, B3);
  or or_5 (S4, A4, B4);
  or or_6 (S5, A5, B5);
  or or_7 (S6, A6, B6);
  or or_8 (SN, AN, BN);
endmodule

module Counter_2 (
  input  E,
  input  CLK,
  input  C,
  output _0,
  output _1
);

  J_K_Flip_Flop #(.trigger("falling")) j_k_ff_1 (.J(E), .clk(CLK), .K(E), .Q(_0), .reset(C));  // open: Qn, preset, en
  J_K_Flip_Flop #(.trigger("falling")) j_k_ff_2 (.J(E), .clk(_0), .K(E), .Q(_1), .reset(C));  // open: Qn, preset, en
endmodule

module Counter_8 (
  input  E,
  input  CLK,
  input  E_2,
  input  C,
  output _0,
  output _1,
  output _2,
  output _3,
  output _4,
  output _5,
  output _6,
  output _7
);

  wire and_1_out;

  and and_1 (and_1_out, CLK, E_2);
  J_K_Flip_Flop #(.trigger("falling")) j_k_ff_1 (
    .J(E), .clk(and_1_out), .K(E), .Q(_0), .reset(C));  // open: Qn, preset, en
  J_K_Flip_Flop #(.trigger("falling")) j_k_ff_2 (.J(E), .clk(_0), .K(E), .Q(_1), .reset(C));  // open: Qn, preset, en
  J_K_Flip_Flop #(.trigger("falling")) j_k_ff_3 (.J(E), .clk(_1), .K(E), .Q(_2), .reset(C));  // open: Qn, preset, en
  J_K_Flip_Flop #(.trigger("falling")) j_k_ff_4 (.J(E), .clk(_2), .K(E), .Q(_3), .reset(C));  // open: Qn, preset, en
  J_K_Flip_Flop #(.trigger("falling")) j_k_ff_5 (.J(E), .clk(_3), .K(E), .Q(_4), .reset(C));  // open: Qn, preset, en
  J_K_Flip_Flop #(.trigger("falling")) j_k_ff_6 (.J(E), .clk(_4), .K(E), .Q(_5), .reset(C));  // open: Qn, preset, en
  J_K_Flip_Flop #(.trigger("falling")) j_k_ff_7 (.J(E), .clk(_5), .K(E), .Q(_6), .reset(C));  // open: Qn, preset, en
  J_K_Flip_Flop #(.trigger("falling")) j_k_ff_8 (.J(E), .clk(_6), .K(E), .Q(_7), .reset(C));  // open: Qn, preset, en
endmodule

module Sub (
  input  A0,
  input  A1,
  input  A2,
  input  A3,
  input  A4,
  input  A5,
  input  A6,
  input  AN,
  output S0,
  output S1,
  output S2,
  output S3,
  output S4,
  output S5,
  output S6,
  output SN,
  output SO
);

  wire not_1_out, not_2_out, not_3_out, not_4_out, not_5_out, not_6_out, not_7_out;

  not not_1 (not_1_out, A0);
  not not_2 (not_2_out, A1);
  not not_3 (not_3_out, A2);
  not not_4 (not_4_out, A3);
  not not_5 (not_5_out, A4);
  not not_6 (not_6_out, A5);
  not not_7 (not_7_out, A6);
  not not_8 (SN, AN);
  Add_8 add_8_1 (
    .A0(not_1_out), .A1(not_2_out), .A2(not_3_out), .A3(not_4_out), .A4(not_5_out), .A5(not_6_out),
    .A6(not_7_out), .AN(1'b0), .B0(1'b1), .B1(1'b0), .B2(1'b0), .B3(1'b0), .B4(1'b0), .B5(1'b0), .B6(1'b0),
    .BN(1'b0), .S0(S0), .S1(S1), .S2(S2), .S3(S3), .S4(S4), .S5(S5), .S6(S6), .SO(SO));  // open: SN
endmodule

module AddSub (
  input  A0,
  input  A1,
  input  A2,
  input  A3,
  input  A4,
  input  A5,
  input  A6,
  input  AN,
  input  RUN,
  input  CLK,
  input  SUB,
  input  B0,
  input  B1,
  input  B2,
  input  B3,
  input  B4,
  input  B5,
  input  B6,
  input  BN,
  output S0,
  output S1,
  output S2,
  output S3,
  output S4,
  output S5,
  output S6,
  output SN
);

  wire and_1_out, and_2_out, sel_8_1_s0, sel_8_1_s1, sel_8_1_s2, sel_8_1_s3, sel_8_1_s4, sel_8_1_s5,
       sel_8_1_s6, sel_8_1_sn, sub_1_s0, sub_1_s1, sub_1_s2, sub_1_s3, sub_1_s4, sub_1_s5, sub_1_s6,
       sub_1_sn, sw_8_1_s0, sw_8_1_s1, sw_8_1_s2, sw_8_1_s3, sw_8_1_s4, sw_8_1_s5, sw_8_1_s6, sw_8_1_sn,
       sw_8_2_s0, sw_8_2_s1, sw_8_2_s2, sw_8_2_s3, sw_8_2_s4, sw_8_2_s5, sw_8_2_s6, sw_8_2_sn;

  and and_1 (and_1_out, RUN, CLK);
  and and_2 (and_2_out, and_1_out, SUB);
  SW_8 sw_8_1 (
    .A0(B0), .A1(B1), .A2(B2), .A3(B3), .A4(B4), .A5(B5), .A6(B6), .AN(BN), .S(and_1_out), .S0(sw_8_1_s0),
    .S1(sw_8_1_s1), .S2(sw_8_1_s2), .S3(sw_8_1_s3), .S4(sw_8_1_s4), .S5(sw_8_1_s5), .S6(sw_8_1_s6),
    .SN(sw_8_1_sn));
  SW_8 sw_8_2 (
    .A0(AN), .A1(A6), .A2(A5), .A3(A4), .A4(A3), .A5(A2), .A6(A1), .AN(A0), .S(and_1_out), .S0(sw_8_2_s0),
    .S1(sw_8_2_s1), .S2(sw_8_2_s2), .S3(sw_8_2_s3), .S4(sw_8_2_s4), .S5(sw_8_2_s5), .S6(sw_8_2_s6),
    .SN(sw_8_2_sn));
  Sub sub_1 (
    .A0(sw_8_1_s0), .A1(sw_8_1_s1), .A2(sw_8_1_s2), .A3(sw_8_1_s3), .A4(sw_8_1_s4), .A5(sw_8_1_s5),
    .A6(sw_8_1_s6), .AN(sw_8_1_sn), .S0(sub_1_s0), .S1(sub_1_s1), .S2(sub_1_s2), .S3(sub_1_s3),
    .S4(sub_1_s4), .S5(sub_1_s5), .S6(sub_1_s6), .SN(sub_1_sn));  // open: SO
  Sel_8 sel_8_1 (
    .A0(sw_8_1_s0), .A1(sw_8_1_s1), .A2(sw_8_1_s2), .A3(sw_8_1_s3), .A4(sw_8_1_s4), .A5(sw_8_1_s5),
    .A6(sw_8_1_s6), .AN(sw_8_1_sn), .B0(sub_1_s0), .B1(sub_1_s1), .B2(sub_1_s2), .B3(sub_1_s3),
    .B4(sub_1_s4), .B5(sub_1_s5), .B6(sub_1_s6), .BN(sub_1_sn), .S(and_2_out), .S0(sel_8_1_s0),
    .S1(sel_8_1_s1), .S2(sel_8_1_s2), .S3(sel_8_1_s3), .S4(sel_8_1_s4), .S5(sel_8_1_s5), .S6(sel_8_1_s6),
    .SN(sel_8_1_sn));
  Add_8 add_8_1 (
    .A0(sw_8_2_sn), .A1(sw_8_2_s6), .A2(sw_8_2_s5), .A3(sw_8_2_s4), .A4(sw_8_2_s3), .A5(sw_8_2_s2),
    .A6(sw_8_2_s1), .AN(sw_8_2_s0), .B0(sel_8_1_s0), .B1(sel_8_1_s1), .B2(sel_8_1_s2), .B3(sel_8_1_s3),
    .B4(sel_8_1_s4), .B5(sel_8_1_s5), .B6(sel_8_1_s6), .BN(sel_8_1_sn), .S0(S0), .S1(S1), .S2(S2), .S3(S3),
    .S4(S4), .S5(S5), .S6(S6), .SN(SN));  // open: SO
endmodule

module Buffer (
  input  [7:0] C,
  input  [7:0] D1,
  input  [7:0] D2,
  input  CLK,
  input  W,
  output [3:0] P,
  output [3:0] C_2,
  output [7:0] D1_2,
  output [7:0] D2_2
);

  wire not_1_out;
  wire [7:0] C2_u, C3_u, C4_u, C5_u, CT2_u, CT3_u, CT4_u, CT5_u, D1CT4_u, D1T2_u, D1T3_u, D1T5_u, D2T2_u,
       D2T3_u, D2T4_u, D2T5_u, D12_u, D13_u, D14_u, D15_u, D22_u, D23_u, D24_u, D25_u;

  D_8 C5 (.D(C), .CLK(CLK), .E(W), .U(C5_u));
  D_8 D15 (.D(D1), .CLK(CLK), .E(W), .U(D15_u));
  D_8 D25 (.D(D2), .CLK(CLK), .E(W), .U(D25_u));
  D_8 CT5 (.D(C5_u), .CLK(not_1_out), .E(W), .U(CT5_u));
  D_8 D1T5 (.D(D15_u), .CLK(not_1_out), .E(W), .U(D1T5_u));
  D_8 D2T5 (.D(D25_u), .CLK(not_1_out), .E(W), .U(D2T5_u));
  not not_1 (not_1_out, CLK);
  D_8 CT4 (.D(C4_u), .CLK(not_1_out), .E(W), .U(CT4_u));
  D_8 C4 (.D(CT5_u), .CLK(CLK), .E(W), .U(C4_u));
  D_8 D1CT4 (.D(D14_u), .CLK(not_1_out), .E(W), .U(D1CT4_u));
  D_8 D14 (.D(D1T5_u), .CLK(CLK), .E(W), .U(D14_u));
  D_8 D2T4 (.D(D24_u), .CLK(not_1_out), .E(W), .U(D2T4_u));
  D_8 D24 (.D(D2T5_u), .CLK(CLK), .E(W), .U(D24_u));
  D_8 C3 (.D(CT4_u), .CLK(CLK), .E(W), .U(C3_u));
  D_8 D13 (.D(D1CT4_u), .CLK(CLK), .E(W), .U(D13_u));
  D_8 D23 (.D(D2T4_u), .CLK(CLK), .E(W), .U(D23_u));
  D_8 CT3 (.D(C3_u), .CLK(not_1_out), .E(W), .U(CT3_u));
  D_8 C2 (.D(CT3_u), .CLK(CLK), .E(W), .U(C2_u));
  D_8 D1T3 (.D(D13_u), .CLK(not_1_out), .E(W), .U(D1T3_u));
  D_8 D12 (.D(D1T3_u), .CLK(CLK), .E(W), .U(D12_u));
  D_8 D2T3 (.D(D23_u), .CLK(not_1_out), .E(W), .U(D2T3_u));
  D_8 D22 (.D(D2T3_u), .CLK(CLK), .E(W), .U(D22_u));
  D_8 C1 (.D(CT2_u), .CLK(CLK), .E(W), .U({C_2, P}));
  D_8 CT2 (.D(C2_u), .CLK(not_1_out), .E(W), .U(CT2_u));
  D_8 D11 (.D(D1T2_u), .CLK(CLK), .E(W), .U(D1_2));
  D_8 D1T2 (.D(D12_u), .CLK(not_1_out), .E(W), .U(D1T2_u));
  D_8 D2T2 (.D(D22_u), .CLK(not_1_out), .E(W), .U(D2T2_u));
  D_8 D21 (.D(D2T2_u), .CLK(CLK), .E(W), .U(D2_2));
endmodule

module PU (
  input  [7:0] D1,
  input  [3:0] C,
  input  CLK,
  input  [7:0] D2,
  output [7:0] O
);

  wire and_1_out, not_1_out, or_1_out, or_2_out, sel_8_1_s0, sel_8_1_s1, sel_8_1_s2, sel_8_1_s3, sel_8_1_s4,
       sel_8_1_s5, sel_8_1_s6, sel_8_1_sn;
  wire [7:0] addsub_1_s0, counter_8_1__0, D1_u, D2_u, nand_1_out, sel_8_2_s0, sel_8_m_1_s_2, sel_8_m_2_s_2,
       sel_8_m_3_s_2, sel_8_m_4_s_2, sw_8_m_1_s_2, undriven, undriven_2, undriven_3;

  and and_1 (and_1_out, C[3], CLK);
  Sel_8_M sel_8_m_1 (.A(D1), .B(addsub_1_s0), .S(or_1_out), .S_2(sel_8_m_1_s_2));
  D_8 u_D1 (.D(sel_8_m_1_s_2), .CLK(CLK), .E(C[1]), .U(D1_u));
  Sel_8_M sel_8_m_2 (.A(D1), .B(D1_u), .S(C[1]), .S_2(sel_8_m_2_s_2));
  Sel_8 sel_8_1 (
    .A0(D2[0]), .A1(D2[1]), .A2(D2[2]), .A3(D2[3]), .A4(D2[4]), .A5(D2[5]), .A6(D2[6]), .AN(D2[7]),
    .B0(sel_8_m_3_s_2[0]), .B1(sel_8_m_3_s_2[1]), .B2(sel_8_m_3_s_2[2]), .B3(sel_8_m_3_s_2[3]),
    .B4(sel_8_m_3_s_2[4]), .B5(sel_8_m_3_s_2[5]), .B6(sel_8_m_3_s_2[6]), .BN(sel_8_m_3_s_2[7]), .S(C[1]),
    .S0(sel_8_1_s0), .S1(sel_8_1_s1), .S2(sel_8_1_s2), .S3(sel_8_1_s3), .S4(sel_8_1_s4), .S5(sel_8_1_s5),
    .S6(sel_8_1_s6), .SN(sel_8_1_sn));
  AddSub addsub_1 (
    .RUN(and_1_out), .CLK(and_1_out), .SUB(C[0]), .A0(sel_8_m_2_s_2[0]), .A1(sel_8_m_2_s_2[1]),
    .A2(sel_8_m_2_s_2[2]), .A3(sel_8_m_2_s_2[3]), .A4(sel_8_m_2_s_2[4]), .A5(sel_8_m_2_s_2[5]),
    .A6(sel_8_m_2_s_2[6]), .AN(sel_8_m_2_s_2[7]), .B0(sel_8_1_s0), .B1(sel_8_1_s1), .B2(sel_8_1_s2),
    .B3(sel_8_1_s3), .B4(sel_8_1_s4), .B5(sel_8_1_s5), .B6(sel_8_1_s6), .BN(sel_8_1_sn), .S0(addsub_1_s0[0]),
    .S1(addsub_1_s0[1]), .S2(addsub_1_s0[2]), .S3(addsub_1_s0[3]), .S4(addsub_1_s0[4]), .S5(addsub_1_s0[5]),
    .S6(addsub_1_s0[6]), .SN(addsub_1_s0[7]));
  Sel_8_M sel_8_m_3 (.A(D2_u), .B(undriven), .S(C[0]), .S_2(sel_8_m_3_s_2));
  D_8 u_D2 (.D(D2), .CLK(CLK), .E(C[0]), .U(D2_u));
  SW_8_M sw_8_m_1 (.B(D1), .S(or_1_out), .S_2(sw_8_m_1_s_2));
  D_8 d_8_1 (.D(undriven), .CLK(CLK), .E(C[0]), .U(sw_8_m_1_s_2));
  assign nand_1_out = ~(D2 & counter_8_1__0);  // NAND_Gate nand_1, 8 bits wide
  or or_1 (or_1_out, counter_8_1__0[7], counter_8_1__0[6], counter_8_1__0[5], counter_8_1__0[4], counter_8_1__0[3], counter_8_1__0[2], counter_8_1__0[1], counter_8_1__0[0]);
  or or_2 (or_2_out, nand_1_out[0], nand_1_out[1], nand_1_out[2], nand_1_out[3], nand_1_out[4], nand_1_out[5], nand_1_out[6], nand_1_out[7]);
  Sel_8_M sel_8_m_4 (.A(sel_8_m_1_s_2), .B(counter_8_1__0), .S(not_1_out), .S_2(sel_8_m_4_s_2));
  not not_1 (not_1_out, or_2_out);
  Counter_8 counter_8_1 (
    .E(or_2_out), .CLK(CLK), .E_2(C[0]), ._0(counter_8_1__0[0]), ._1(counter_8_1__0[1]),
    ._2(counter_8_1__0[2]), ._3(counter_8_1__0[3]), ._4(counter_8_1__0[4]), ._5(counter_8_1__0[5]),
    ._6(counter_8_1__0[6]), ._7(counter_8_1__0[7]));  // open: C
  Sel_8 sel_8_2 (
    .A0(undriven_3[0]), .A1(undriven_3[1]), .A2(undriven_3[2]), .A3(undriven_3[3]), .A4(undriven_3[4]),
    .A5(undriven_3[5]), .A6(undriven_3[6]), .AN(undriven_3[7]), .B0(undriven_2[7]), .B1(undriven_2[6]),
    .B2(undriven_2[5]), .B3(undriven_2[4]), .B4(undriven_2[3]), .B5(undriven_2[2]), .B6(undriven_2[1]),
    .BN(undriven_2[0]), .S0(sel_8_2_s0[0]), .S1(sel_8_2_s0[1]), .S2(sel_8_2_s0[2]), .S3(sel_8_2_s0[3]),
    .S4(sel_8_2_s0[4]), .S5(sel_8_2_s0[5]), .S6(sel_8_2_s0[6]), .SN(sel_8_2_s0[7]));  // open: S
  Sel_8 sel_8_3 (
    .A0(addsub_1_s0[0]), .A1(addsub_1_s0[1]), .A2(addsub_1_s0[2]), .A3(addsub_1_s0[3]), .A4(addsub_1_s0[4]),
    .A5(addsub_1_s0[5]), .A6(addsub_1_s0[6]), .AN(addsub_1_s0[7]), .B0(sel_8_m_4_s_2[0]),
    .B1(sel_8_m_4_s_2[1]), .B2(sel_8_m_4_s_2[2]), .B3(sel_8_m_4_s_2[3]), .B4(sel_8_m_4_s_2[4]),
    .B5(sel_8_m_4_s_2[5]), .B6(sel_8_m_4_s_2[6]), .BN(sel_8_m_4_s_2[7]), .S(C[1]), .S0(O[0]), .S1(O[1]),
    .S2(O[2]), .S3(O[3]), .S4(O[4]), .S5(O[5]), .S6(O[6]), .SN(O[7]));
endmodule

module CPU (
  input  C0,
  input  C1,
  input  C2,
  input  C3,
  input  C4,
  input  C5,
  input  C6,
  input  C7,
  input  D10,
  input  D11,
  input  D12,
  input  D13,
  input  D14,
  input  D15,
  input  D16,
  input  D17,
  input  D20,
  input  D21,
  input  D22,
  input  D23,
  input  D24,
  input  D25,
  input  D26,
  input  D27
);
endmodule
